// Logisim project Last.circ as structural Verilog: 1 circuit, main circuit main
module main (
);

  wire cdm_16_1_p2, cdm_16_1_p3, cdm_16_1_p5, cdm_16_1_p6, cdm_16_1_p7, cdm_16_1_p8, cdm_16_1_p9,
       cdm_16_1_p10, cdm_16_1_p11, clock, mem, not_1_out, ram_1_p1, ram_1_p3, ram_1_p11, read, word;
  wire [7:0] ram_1_p5;
  wire [15:0] address_bus, cdm_16_1_p16, cdm_16_1_p17, data_bus;

  // Debugger debugger_1: pin names not known
  // Probe on cdm_16_1_p3
  // Probe on cdm_16_1_p2
  // Probe on cdm_16_1_p5
  // Probe on cdm_16_1_p6
  // CdM_16 cdm_16_1: pin names not known; wires that end beside it: 6'b000101, cdm_16_1_p2, cdm_16_1_p3, clock, cdm_16_1_p5, cdm_16_1_p6, cdm_16_1_p7, cdm_16_1_p8, cdm_16_1_p9, cdm_16_1_p10, cdm_16_1_p11, mem, read, word, address_bus, cdm_16_1_p16, cdm_16_1_p17
  Clock clock_1 (.out(clock));
  // Probe on cdm_16_1_p8
  // Probe on cdm_16_1_p7
  // Probe on cdm_16_1_p9
  // Probe on cdm_16_1_p10
  // Probe on cdm_16_1_p11
  assign cdm_16_1_p17 = read ? data_bus : 16'bz;  // Controlled_Buffer controlled_buffer_1
  assign data_bus = not_1_out ? cdm_16_1_p16 : 16'bz;  // Controlled_Buffer controlled_buffer_2
  not not_1 (not_1_out, read);
  // RAM ram_1: pin names not known; wires that end beside it: ram_1_p1, ram_1_p1, ram_1_p3, address_bus, ram_1_p5, word, mem, clock, ram_1_p3, read, ram_1_p11, data_bus
  LED led_1 (.in(ram_1_p11));
endmodule
